// Logisim project Grupo1.circ as structural Verilog: 1 circuit, main circuit ULA
module ULA (
  input  A3,
  input  A2,
  input  A1,
  input  A0,
  input  B3,
  input  B2,
  input  B1,
  input  B0,
  input  E1,
  input  E0,
  output out_11,
  output out_12,
  output out_13,
  output out_14,
  output out_15,
  output out_16
);

  wire bcd_1_a, bcd_1_b, bcd_1_c, bcd_1_d, bcd_1_e, bcd_1_f, bcd_1_g, bcd_2_a, bcd_2_b, bcd_2_c, bcd_2_d,
       bcd_2_e, bcd_2_f, bcd_2_g, bcd_3_a, bcd_3_b, bcd_3_c, bcd_3_d, bcd_3_e, bcd_3_f, bcd_3_g, or_1_out;
  wire [3:0] main_1_out_9, main_2_out_9, somador_1_s3, subtrator_1_s3;

  BCD bcd_1 (
    .E3(B3), .E2(B2), .E1(B1), .E0(B0), .a(bcd_1_a), .b(bcd_1_b), .c(bcd_1_c), .d(bcd_1_d), .e(bcd_1_e),
    .f(bcd_1_f), .g(bcd_1_g));
  _7_Segment_Display u_7_segment_display_1 (
    .g(bcd_1_g), .f(bcd_1_f), .a(bcd_1_a), .b(bcd_1_b), .e(bcd_1_e), .d(bcd_1_d), .c(bcd_1_c));  // open: dp
  _7_Segment_Display u_7_segment_display_2 (
    .g(bcd_2_g), .f(bcd_2_f), .a(bcd_2_a), .b(bcd_2_b), .e(bcd_2_e), .d(bcd_2_d), .c(bcd_2_c));  // open: dp
  BCD bcd_2 (
    .E3(A3), .E2(A2), .E1(A1), .E0(A0), .a(bcd_2_a), .b(bcd_2_b), .c(bcd_2_c), .d(bcd_2_d), .e(bcd_2_e),
    .f(bcd_2_f), .g(bcd_2_g));
  Somador somador_1 (
    .A3(A3), .A2(A2), .A1(A1), .A0(A0), .B3(B3), .B2(B2), .B1(B1), .B0(B0), .Cout(out_11),
    .S2(somador_1_s3[1]), .S1(somador_1_s3[2]), .S0(somador_1_s3[3]), .S3(somador_1_s3[0]));  // open: Cin
  Subtrator subtrator_1 (
    .A3(A3), .A2(A2), .A1(A1), .B3(B3), .A0(A0), .B2(B2), .B1(B1), .B0(B0), .S3(subtrator_1_s3[0]),
    .S2(subtrator_1_s3[1]), .S1(subtrator_1_s3[2]), .S0(subtrator_1_s3[3]), .Cout(out_16));
  AND_main main_1 (
    .in_1(A3), .in_2(A2), .in_3(A1), .in_4(A0), .in_5(B3), .in_6(B2), .in_7(B1), .in_8(B0),
    .out_9(main_1_out_9[0]), .out_10(main_1_out_9[1]), .out_11(main_1_out_9[2]), .out_12(main_1_out_9[3]));
  OR_main main_2 (
    .in_1(A3), .in_2(A2), .in_3(A1), .in_4(A0), .in_5(B3), .in_6(B2), .in_7(B1), .in_8(B0),
    .out_9(main_2_out_9[0]), .out_10(main_2_out_9[1]), .out_11(main_2_out_9[2]), .out_12(main_2_out_9[3]));
  Multiplexer #(.select(2), .width(4), .enable("false")) multiplexer_1 (
    .in0(somador_1_s3), .in1(subtrator_1_s3), .in2(main_1_out_9), .in3(main_2_out_9),
    .out({out_15, out_14, out_13, out_12}), .sel({E1, E0}));
  BCD bcd_3 (
    .E3(out_12), .E2(out_13), .E1(out_14), .E0(out_15), .a(bcd_3_a), .b(bcd_3_b), .c(bcd_3_c), .d(bcd_3_d),
    .e(bcd_3_e), .f(bcd_3_f), .g(bcd_3_g));
  or or_1 (or_1_out, out_12, out_13, out_14, out_15);
  _7_Segment_Display u_7_segment_display_3 (
    .g(bcd_3_g), .f(bcd_3_f), .a(bcd_3_a), .b(bcd_3_b), .e(bcd_3_e), .d(bcd_3_d), .c(bcd_3_c));  // open: dp
  LED #(.active("false")) ZERO (.in(or_1_out));
endmodule
