// Logisim project Somador.circ as structural Verilog: 1 circuit, main circuit Somador
module Somador (
  input  A3,
  input  A2,
  input  A1,
  input  Cin,
  input  A0,
  input  B3,
  input  B2,
  input  B1,
  input  B0,
  output S3,
  output S2,
  output S1,
  output S0,
  output Cout
);

  Adder #(.width(4)) adder_1 (
    .a({A3, A2, A1, A0}), .b({B3, B2, B1, B0}), .out({S3, S2, S1, S0}), .cin(Cin), .cout(Cout));
endmodule
