// Logisim project Subtrator.circ as structural Verilog: 1 circuit, main circuit Subtrator
module Subtrator (
  input  A3,
  input  A2,
  input  A1,
  input  B3,
  input  A0,
  input  B2,
  input  B1,
  input  B0,
  output S3,
  output S2,
  output S1,
  output S0,
  output Cout
);

  wire [3:0] xor_4_out;

  xor xor_1 (xor_4_out[3], B3, 1'b1);
  xor xor_2 (xor_4_out[2], B2, 1'b1);
  xor xor_3 (xor_4_out[1], B1, 1'b1);
  xor xor_4 (xor_4_out[0], B0, 1'b1);
  Adder #(.width(4)) adder_1 (.a({A3, A2, A1, A0}), .b(xor_4_out), .out({S3, S2, S1, S0}), .cin(1'b1), .cout(Cout));

  // Notes on the sheet:
  //   Somador e subtrator com display
endmodule
