// Logisim project COD E DEC.circ as structural Verilog: 1 circuit, main circuit main
module main (
  input  in_1,
  input  in_2,
  input  in_3,
  input  in_4,
  output Dec_2x4,
  output out_6,
  output out_7,
  output out_8
);

  wire cod_4x2_1_s0, cod_4x2_1_s1;

  COD_4X2 cod_4x2_1 (.E3(in_1), .E2(in_2), .E1(in_3), .E0(in_4), .S1(cod_4x2_1_s1), .S0(cod_4x2_1_s0));
  DEC_2X4 dec_2x4_1 (.E1(cod_4x2_1_s1), .E0(cod_4x2_1_s0), .S3(Dec_2x4), .S2(out_6), .S1(out_7), .S0(out_8));
endmodule
