// Logisim project Codificador 4X2.circ as structural Verilog: 1 circuit, main circuit COD 4X2
module COD_4X2 (
  input  E3,
  input  E2,
  input  E1,
  input  E0,
  output S1,
  output S0
);

  or or_1 (S1, E3, E2);
  or or_2 (S0, E3, E1);
endmodule
