// Logisim project Codificador BCD.circ as structural Verilog: 1 circuit, main circuit COD BCD
module COD_BCD (
  input  E9,
  input  E8,
  input  E7,
  input  E6,
  input  E5,
  input  E4,
  input  E3,
  input  E2,
  input  E1,
  input  E0,
  output S3,
  output S2,
  output S1,
  output S0
);

  or or_1 (S3, E9, E8);
  or or_2 (S2, E7, E6, E5, E4);
  or or_3 (S1, E7, E6, E3, E2);
  or or_4 (S0, E9, E7, E5, E3, E1);
endmodule
