// Logisim project DISPLAY 0 - 9.circ as structural Verilog: 1 circuit, main circuit main
module main (
  input  in_1,
  input  in_2,
  input  in_3,
  input  in_4,
  input  in_5,
  input  in_6,
  input  in_7,
  input  in_8,
  input  in_9,
  input  in_10
);

  wire cod_bcd_1_s0, cod_bcd_1_s1, cod_bcd_1_s2, cod_bcd_1_s3, dec_bcd_display_1_a, dec_bcd_display_1_b,
       dec_bcd_display_1_c, dec_bcd_display_1_d, dec_bcd_display_1_e, dec_bcd_display_1_f,
       dec_bcd_display_1_g;

  COD_BCD cod_bcd_1 (
    .E9(in_1), .E8(in_2), .E7(in_3), .E6(in_4), .E5(in_5), .S3(cod_bcd_1_s3), .S2(cod_bcd_1_s2),
    .S1(cod_bcd_1_s1), .S0(cod_bcd_1_s0), .E3(in_7), .E2(in_8), .E1(in_9), .E0(in_10), .E4(in_6));
  Dec_BCD_display dec_bcd_display_1 (
    .E3(cod_bcd_1_s3), .E2(cod_bcd_1_s2), .E1(cod_bcd_1_s1), .E0(cod_bcd_1_s0), .a(dec_bcd_display_1_a),
    .b(dec_bcd_display_1_b), .c(dec_bcd_display_1_c), .d(dec_bcd_display_1_d), .e(dec_bcd_display_1_e),
    .f(dec_bcd_display_1_f), .g(dec_bcd_display_1_g));
  _7_Segment_Display u_7_segment_display_1 (
    .g(dec_bcd_display_1_g), .f(dec_bcd_display_1_f), .a(dec_bcd_display_1_a), .b(dec_bcd_display_1_b),
    .e(dec_bcd_display_1_e), .d(dec_bcd_display_1_d), .c(dec_bcd_display_1_c));  // open: dp
endmodule
