// Logisim project Decodificador 2x4.circ as structural Verilog: 1 circuit, main circuit DEC 2X4
module DEC_2X4 (
  input  E1,
  input  E0,
  output S3,
  output S2,
  output S1,
  output S0
);

  wire not_1_out, not_2_out, not_3_out, not_4_out;

  and and_1 (S3, E1, E0);
  not not_1 (not_1_out, E0);
  not not_2 (not_2_out, E1);
  not not_3 (not_3_out, E1);
  not not_4 (not_4_out, E0);
  and and_2 (S2, E1, not_1_out);
  and and_3 (S1, not_2_out, E0);
  and and_4 (S0, not_3_out, not_4_out);
endmodule
