// Logisim project display 7 segmentos funcionando.circ as structural Verilog: 1 circuit, main circuit main
module main (
  input  in_1,
  input  in_2,
  input  in_3,
  input  in_4
);

  wire dec_bcd_display_1_a, dec_bcd_display_1_b, dec_bcd_display_1_c, dec_bcd_display_1_d,
       dec_bcd_display_1_e, dec_bcd_display_1_f, dec_bcd_display_1_g;

  Dec_BCD_display dec_bcd_display_1 (
    .E3(in_1), .E2(in_2), .E1(in_3), .E0(in_4), .a(dec_bcd_display_1_a), .b(dec_bcd_display_1_b),
    .c(dec_bcd_display_1_c), .d(dec_bcd_display_1_d), .e(dec_bcd_display_1_e), .f(dec_bcd_display_1_f),
    .g(dec_bcd_display_1_g));
  _7_Segment_Display u_7_segment_display_1 (
    .g(dec_bcd_display_1_g), .f(dec_bcd_display_1_f), .a(dec_bcd_display_1_a), .b(dec_bcd_display_1_b),
    .e(dec_bcd_display_1_e), .d(dec_bcd_display_1_d), .c(dec_bcd_display_1_c));  // open: dp
endmodule
