// Logisim project teste display 7 segmentos.circ as structural Verilog: 1 circuit, main circuit main
module main (
  input  in_1,
  input  in_2,
  input  in_3,
  input  in_4,
  input  in_5,
  input  in_6,
  input  in_7,
  input  in_8
);

  _7_Segment_Display u_7_segment_display_1 (
    .g(in_1), .f(in_2), .a(in_3), .b(in_4), .e(in_5), .d(in_6), .c(in_7), .dp(in_8));
endmodule
