// Logisim project MUX.circ as structural Verilog: 1 circuit, main circuit main
module main (
  input  I0,
  input  I0_2,
  input  I1,
  input  I2,
  input  I1_2,
  input  I3,
  input  Enable,
  input  I2_2,
  input  A,
  input  B,
  input  I3_2,
  input  A_2,
  input  B_2,
  output Z,
  output Z_2
);

  wire and_1_out, and_2_out, and_3_out, and_4_out, not_1_out, not_2_out;

  Multiplexer #(.select(2), .disabled(0)) multiplexer_1 (
    .in0(I0_2), .in1(I1), .in2(I2), .in3(I3), .out(Z), .sel({A, B}), .en(Enable));
  not not_1 (not_1_out, A_2);
  not not_2 (not_2_out, B_2);
  and and_1 (and_1_out, I0, not_1_out, not_2_out);
  and and_2 (and_2_out, I1_2, not_1_out, B_2);
  and and_3 (and_3_out, I2_2, A_2, not_2_out);
  and and_4 (and_4_out, I3_2, A_2, B_2);
  or or_1 (Z_2, and_1_out, and_2_out, and_3_out, and_4_out);
endmodule
