// Logisim project Full Subtractor.circ as structural Verilog: 1 circuit, main circuit main
module main (
  input  A,
  input  B,
  input  Bi,
  output \Diferença ,
  output Bo
);

  wire and_1_out, and_2_out, not_1_out, not_2_out, xor_1_out;

  xor xor_1 (xor_1_out, A, B);
  not not_1 (not_1_out, A);
  and and_1 (and_1_out, not_1_out, B);
  not not_2 (not_2_out, xor_1_out);
  xor xor_2 (\Diferença , xor_1_out, Bi);
  and and_2 (and_2_out, not_2_out, Bi);
  or or_1 (Bo, and_2_out, and_1_out);
endmodule
