// Logisim project Somador e Subtrator em C2.circ as structural Verilog: 1 circuit, main circuit main
module main (
  input  A3,
  input  Sub__1____Soma__0,
  input  A2,
  input  A1,
  input  B3,
  input  A0,
  input  B2,
  input  B1,
  input  B0,
  output S3,
  output S2,
  output S1,
  output S0,
  output Cout
);

  wire [3:0] xor_4_out;

  xor xor_1 (xor_4_out[3], B3, Sub__1____Soma__0);
  xor xor_2 (xor_4_out[2], B2, Sub__1____Soma__0);
  xor xor_3 (xor_4_out[1], B1, Sub__1____Soma__0);
  xor xor_4 (xor_4_out[0], B0, Sub__1____Soma__0);
  Adder #(.width(4)) adder_1 (
    .a({A3, A2, A1, A0}), .b(xor_4_out), .out({S3, S2, S1, S0}), .cin(Sub__1____Soma__0), .cout(Cout));
endmodule
